# Fritzing sketch diagramaBrazo_robotico (saved by Fritzing 0.9.3b)
breadboards: 1

parts:
  J1 = Basic Servo
  J2 = Basic Servo
  J3 = Basic Servo [part_number=1]
  X2 = X113647 Stepper Driver Board [package=board]
  MOTOR2 = 28BYJ-48 Stepper Motor
  Componente1 = Arduino Uno (Rev3) - ICSP
  LED1 = smd LED [color="Red (633nm)" package="0603 [SMD]"]
  LED2 = smd LED [color="Green (570nm)" package="0603 [SMD]"]
  S1 = Momentary Switch [package=ksa_sealed_tac_switch]
  R1 = Resistor [tolerance=±5% resistance=220 package="0402 [SMD]"]
  R2 = Resistor [tolerance=±5% resistance=220 package="0402 [SMD]"]

nets:
  GND: J1.gnd, J2.gnd, J3.gnd, X2.GND, Componente1.GND, LED1.cathode, LED2.cathode
  VCC: J1.vcc, J2.vcc, J3.vcc, X2.+V, Componente1.5V, S1.1
  N1: J1.pulse, Componente1.D9_PWM
  N2: J2.pulse, Componente1.D10_PWM/SS
  N3: J3.pulse, Componente1.D11_PWM/MOSI
  N4: X2.IN1, Componente1.D2, S1.3
  N5: X2.IN2, Componente1.D4
  N6: X2.IN3, Componente1.D5_PWM
  N7: X2.IN4, Componente1.D6_PWM
  N8: X2.BLUE, MOTOR2.BLUE
  N9: X2.PINK, X2.RED, MOTOR2.PINK, MOTOR2.RED
  N10: X2.YELLOW, MOTOR2.YELLOW
  N11: X2.ORANGE, MOTOR2.ORANGE
  N12: Componente1.ICSP_MISO, Componente1.D12/MISO, R2.Pin_1
  N13: Componente1.D13/SCK, R1.Pin_1
  N14: LED1.anode, R1.Pin_0
  N15: LED2.anode, R2.Pin_0

custom parts:
  X113647 Stepper Driver Board: A common stepper motor driver board based on ULN2003APG darlington array
  28BYJ-48 Stepper Motor: 28BYJ-48 gear-reduction stepper motor (small)
